# Fritzing sketch IKEA UPPATVIND Air Purifier (saved by Fritzing 1.0.5)

parts:
  Mod1 = Amica NodeMCU DEVKIT 1.0
  M1 = xy-mos d4184 [package=THT]
  OUT_3_3V_-_IN_24V = RioRand LM2596
  FAN_[FG_PWM_GND_24V] = polarizedheader 4pin 0.156in [package=THT]
  IN_24V = 2.1mm Barrel Jack with Terminal Block

nets:
  N1: Mod1.pin1, Mod1.pin_26, OUT_3_3V_-_IN_24V.Pin_3
  N2: Mod1.pin2, Mod1.pin_9, Mod1.pin_25, M1.pin2, M1.pin7, OUT_3_3V_-_IN_24V.Pin_2, OUT_3_3V_-_IN_24V.Pin_4, IN_24V.NEG
  N3: Mod1.pin8, FAN_[FG_PWM_GND_24V].pin2
  N4: Mod1.pin_14, M1.pin1
  N5: M1.pin8, OUT_3_3V_-_IN_24V.Pin_1, IN_24V.POS
  N6: M1.pin9, FAN_[FG_PWM_GND_24V].pin4
  N7: M1.pin10, FAN_[FG_PWM_GND_24V].pin3

custom parts:
  xy-mos d4184: xy-mos d4184 Two parallel N-Channel logic compatible MOSFETS with low Rds(on) for high current low-side switching applications.
